# Fritzing sketch Fritzing Sketch Source File (saved by Fritzing 0.9.3b)

parts:
  U1 = 2-Channel 5v Relay Shield [package=relay-2ch5v10a]
  Part1 = Arduino Uno (Rev3)
  Part2 = Bluetooth HC-05 Macho
  LED2 = LEDs [package=led10mm]
  LED1 = LEDs [package=led10mm]
  Power_plug1 = Power plug
  Power_plug2 = Power plug

nets:
  VCC: U1.VCC, Part1.5V, Part2.VCC
  GND: U1.GND, Part1.GND, Part2.GND
  N1: U1.IN1, Part1.D6_PWM
  N2: U1.IN2, Part1.D7
  N3: U1.K1-In, LED2.A
  N4: U1.K1-Off, Power_plug2.VCC
  N5: U1.K1-On, U1.K2-In, U1.K2-Off, U1.K2-On, LED1.A, Power_plug1.VCC
  N6: Part1.D10_PWM/SS, Part2.RXD
  N7: Part1.D11_PWM/MOSI, Part2.TXD
  N8: LED2.C, Power_plug2.GND
  N9: LED1.C, Power_plug1.GND

notes:
  GND - Green
  5VC - Red
  GPIO - Blue
  Developed By Web Dev Fusion
  www.webdevfusion.com

custom parts:
  2-Channel 5v Relay Shield: 2 Channel 5v Relay Shield w. 2x SPD-06VDC-SD-C
  LEDs: LEDs Standard schematic elements and footprints for 5mm, 3mm, 1206, and 0603 sized LEDs. 5mm - Spark Fun Electronics SKU : COM-00529 (and others)
